# Fritzing sketch sketch2 (saved by Fritzing 0.9.6b)

parts:
  J1 = male pin header, 2 pins [form="♂ (male)"]
  D1 = Rectifier Diode [part_number=1N4001 package="300 mil [THT]"]
  R1 = Resistor [tolerance=±5% power=0.25 resistance=50k package=THT]
  MOSFET_1 = MOSFET-NCHANNEL [package=to-92]
  Part1 = Adafruit FeatherWing Proto [part_number="Adafruit #2884"]

nets:
  N1: J1.pin1, D1.cathode, Part1.N$64, Part1.N$65
  N2: J1.pin2, D1.anode, MOSFET_1.D, Part1.N$67, Part1.N$68, Part1.N$69
  N3: R1.Pin_0, MOSFET_1.G, Part1.L, Part1.N$72, Part1.N$74
  N4: R1.Pin_1, MOSFET_1.S, Part1.GND, Part1.N$70, Part1.N$71

custom parts:
  MOSFET-NCHANNEL: Generic NMOS footprint
  Adafruit FeatherWing Proto: This is the FeatherWing Proto - a prototyping add-on for all Feather boards. Using our Feather Stacking Headers or Feather Female Headers you can connect a FeatherWing on top or bottom of your Feather board and let the board take flight! This has a duplicate breakout for each pin on a Feather, as well as a bunch of plain grid proto holes. For GND and 3.3V, we give you a strip of connected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
