# Fritzing sketch sketch_bluefruit_32u4 (saved by Fritzing 0.9.6b)

parts:
  J1 = male pin header, 2 pins [form="♂ (male)"]
  R1 = Resistor [tolerance=±5% power=0.25 resistance=47k package=THT]
  Q1 = MOSFET-NCHANNEL [package=to-92]
  Part1 = Adafruit FeatherWing Proto [part_number="Adafruit #2884"]
  D1 = Rectifier Diode [part_number=1N4001 package="300 mil [THT]"]
  J2 = male pin header, 3 pins [form="♂ (male)"]
  R2 = Resistor [tolerance=±5% power=0.25 resistance=100k package=THT]
  Charger = Adafruit BQ24074 Solar-DC-USB Lipo Charger
  R3 = Resistor [tolerance=±5% power=0.25 resistance=100k package=THT]
  R4 = Resistor [tolerance=±5% power=0.25 resistance=100k package=THT]
  BAT/GND/POW/EN/DON = single row smd male pin header, 5 pins [form="♂ (male)"]
  BAT/GND/POW/EN/DON_2 = single row smd female pin header, 5 pins [form="♀ (female)"]
  Power_Timer = Adafruit TPL5111 Reset Enable Timer [part_number="Adafruit #3573"]

nets:
  N1: J1.pin1, Part1.USB, Part1.N$42, Part1.N$64, Part1.N$65, Part1.N$66, D1.cathode, BAT/GND/POW/EN/DON.pin3
  N2: J1.pin2, Q1.D, Part1.N$67, Part1.N$68, Part1.N$69, D1.anode
  N3: R1.Pin_0, Q1.G, Part1.RX, Part1.N$72, Part1.N$73, Part1.N$74
  N4: R1.Pin_1, Q1.S, Part1.GND, Part1.N$43, Part1.N$70, Part1.N$71, J2.pin3, R2.Pin_0, R3.Pin_0, BAT/GND/POW/EN/DON.pin2
  N5: Part1.EN, Part1.N$37, BAT/GND/POW/EN/DON.pin4
  N6: Part1.M, Part1.N$35, R3.Pin_1, R4.Pin_1
  N7: Part1.L, Part1.N$36, BAT/GND/POW/EN/DON.pin5
  N8: Part1.K, Part1.N$30, Part1.N$33, J2.pin1, R2.Pin_1
  N9: Part1.J, Part1.N$91
  N10: Part1.I, Part1.N$101
  N11: Part1.H, Part1.N$111
  N12: Part1.SCL, Part1.N$121
  N13: Part1.SDA, Part1.N$127
  N14: Part1.TX, Part1.N$83
  N15: Part1.F, Part1.N$32
  N16: Part1.E, Part1.N$34
  N17: Part1.D, Part1.N$39
  N18: Part1.C, Part1.N$40
  N19: Part1.B, Part1.N$45
  N20: Part1.A, Part1.N$46
  N21: Part1.3V, J2.pin2
  N22: Part1.N$48, R4.Pin_0, BAT/GND/POW/EN/DON.pin1
  N23: Charger.VLIPO, BAT/GND/POW/EN/DON_2.pin1
  GND: Charger.GND, BAT/GND/POW/EN/DON_2.pin2, Power_Timer.GND
  N24: Charger.OUT, BAT/GND/POW/EN/DON_2.pin3, Power_Timer.VDD
  N25: BAT/GND/POW/EN/DON_2.pin4, Power_Timer.ENOUT
  N26: BAT/GND/POW/EN/DON_2.pin5, Power_Timer.DONE

custom parts:
  MOSFET-NCHANNEL: Generic NMOS footprint
  Adafruit FeatherWing Proto: This is the FeatherWing Proto - a prototyping add-on for all Feather boards. Using our Feather Stacking Headers or Feather Female Headers you can connect a FeatherWing on top or bottom of your Feather board and let the board take flight! This has a duplicate breakout for each pin on a Feather, as well as a bunch of plain grid proto holes. For GND and 3.3V, we give you a strip of connected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
  Adafruit TPL5111 Reset Enable Timer: The Adafruit TPL5111 Reset Enable Timer is a stand-alone breakout that will turn any electronics into low-power electronics! It will take care of enabling & disabling your electronics using a built in timer that can vary from once-every 100ms up to once every two hours. Basically, the TPL will set an enable pin high periodically, adjustable by potentiometer or resistor, and turn on your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
